# Fritzing sketch InnovationAward (saved by Fritzing 0.8.7b)
circuit board: 8.46667cm x 5.64444cm

parts:
  TRINKET1 = Trinket 5V  # not connected
  C1 = Electrolytic Capacitor [capacitance=1000µF package="300 mil [THT, electrolytic]"]  # not connected
  proto1 = Adafruit_PermaProto_1_4_Board
  NEOPIXEL1 = Neopixel Strip -- White (60/m)
  JACK1 = 2.1mm Barrel Jack with Terminal Block
  R1 = Resistor [tolerance=±5% resistance=400 package=THT]  # not connected

nets:
  N1: proto1.connectorA7, proto1.connectorW7
  N2: proto1.connectorA8, proto1.connectorX8
  N3: proto1.connectorG15, NEOPIXEL1.+5V
  N4: proto1.connectorW1, JACK1.POS
  N5: proto1.connectorW14, NEOPIXEL1.DI
  N6: proto1.connectorX1, JACK1.NEG
  N7: proto1.connectorX13, NEOPIXEL1.GND

custom parts:
  Trinket 5V: Adafruit Trinket 5V
  Neopixel Strip -- White (60/m): Neopixel Strip, White, 60 pixels per meter.
